// Logisim project nincpu.circ as structural Verilog
module HalfAdder (
  input  Ax,
  input  Bx,
  output Carry,
  output Res
);

  and and_1 (Carry, Bx, Ax);
  or or_1 (Res, Ax, Bx);
endmodule
