// Logisim project nincpu_mem.circ as structural Verilog
module sixteenRegister (
  input  WriteEnable,
  input  Clk,
  input  OutputEnable,
  input  Selected,
  input  [15:0] DataIn,
  output [15:0] DataOut
);

  wire and_1_out, and_2_out, and_3_out, and_4_out, and_5_out, and_6_out, and_7_out, and_8_out, and_9_out,
       and_10_out, and_11_out, and_12_out, and_13_out, and_14_out, and_15_out, and_16_out, and_17_out,
       and_18_out, and_19_out, and_20_out, and_21_out, and_22_out, and_23_out, and_24_out, and_25_out,
       and_26_out, and_27_out, and_28_out, and_29_out, and_30_out, and_31_out, and_32_out, and_33_out,
       and_34_out, j_k_ff_1_q, j_k_ff_2_q, j_k_ff_3_q, j_k_ff_4_q, j_k_ff_5_q, j_k_ff_6_q, j_k_ff_7_q,
       j_k_ff_8_q, j_k_ff_9_q, j_k_ff_10_q, j_k_ff_11_q, j_k_ff_12_q, j_k_ff_13_q, j_k_ff_14_q, j_k_ff_15_q,
       j_k_ff_16_q;

  and and_1 (and_1_out, Selected, WriteEnable);
  and and_2 (and_2_out, DataIn[0], and_1_out);
  and and_3 (and_3_out, DataIn[1], and_1_out);
  and and_4 (and_4_out, DataIn[2], and_1_out);
  and and_5 (and_5_out, DataIn[3], and_1_out);
  and and_6 (and_6_out, DataIn[4], and_1_out);
  and and_7 (and_7_out, DataIn[5], and_1_out);
  and and_8 (and_8_out, DataIn[6], and_1_out);
  and and_9 (and_9_out, DataIn[7], and_1_out);
  and and_10 (and_10_out, DataIn[8], and_1_out);
  and and_11 (and_11_out, DataIn[9], and_1_out);
  and and_12 (and_12_out, DataIn[10], and_1_out);
  and and_13 (and_13_out, DataIn[11], and_1_out);
  and and_14 (and_14_out, DataIn[12], and_1_out);
  and and_15 (and_15_out, DataIn[13], and_1_out);
  and and_16 (and_16_out, DataIn[14], and_1_out);
  and and_17 (and_17_out, DataIn[15], and_1_out);
  and and_18 (and_18_out, ~DataIn[0], and_1_out);  // AND_Gate
  and and_19 (and_19_out, ~DataIn[1], and_1_out);  // AND_Gate
  and and_20 (and_20_out, ~DataIn[2], and_1_out);  // AND_Gate
  and and_21 (and_21_out, ~DataIn[3], and_1_out);  // AND_Gate
  and and_22 (and_22_out, ~DataIn[4], and_1_out);  // AND_Gate
  and and_23 (and_23_out, ~DataIn[5], and_1_out);  // AND_Gate
  and and_24 (and_24_out, ~DataIn[6], and_1_out);  // AND_Gate
  and and_25 (and_25_out, ~DataIn[7], and_1_out);  // AND_Gate
  and and_26 (and_26_out, ~DataIn[8], and_1_out);  // AND_Gate
  and and_27 (and_27_out, ~DataIn[9], and_1_out);  // AND_Gate
  and and_28 (and_28_out, ~DataIn[10], and_1_out);  // AND_Gate
  and and_29 (and_29_out, ~DataIn[11], and_1_out);  // AND_Gate
  and and_30 (and_30_out, ~DataIn[12], and_1_out);  // AND_Gate
  and and_31 (and_31_out, ~DataIn[13], and_1_out);  // AND_Gate
  and and_32 (and_32_out, ~DataIn[14], and_1_out);  // AND_Gate
  and and_33 (and_33_out, ~DataIn[15], and_1_out);  // AND_Gate
  and and_34 (and_34_out, Selected, OutputEnable);
  J_K_Flip_Flop j_k_ff_1 (.J(and_2_out), .K(and_18_out), .clk(Clk), .Q(j_k_ff_1_q));  // open: Qn, preset, reset
  J_K_Flip_Flop j_k_ff_2 (.J(and_3_out), .K(and_19_out), .clk(Clk), .Q(j_k_ff_2_q));  // open: Qn, preset, reset
  J_K_Flip_Flop j_k_ff_3 (.J(and_4_out), .K(and_20_out), .clk(Clk), .Q(j_k_ff_3_q));  // open: Qn, preset, reset
  J_K_Flip_Flop j_k_ff_4 (.J(and_5_out), .K(and_21_out), .clk(Clk), .Q(j_k_ff_4_q));  // open: Qn, preset, reset
  J_K_Flip_Flop j_k_ff_5 (.J(and_6_out), .K(and_22_out), .clk(Clk), .Q(j_k_ff_5_q));  // open: Qn, preset, reset
  J_K_Flip_Flop j_k_ff_6 (.J(and_7_out), .K(and_23_out), .clk(Clk), .Q(j_k_ff_6_q));  // open: Qn, preset, reset
  J_K_Flip_Flop j_k_ff_7 (.J(and_8_out), .K(and_24_out), .clk(Clk), .Q(j_k_ff_7_q));  // open: Qn, preset, reset
  J_K_Flip_Flop j_k_ff_8 (.J(and_9_out), .K(and_25_out), .clk(Clk), .Q(j_k_ff_8_q));  // open: Qn, preset, reset
  J_K_Flip_Flop j_k_ff_9 (.J(and_10_out), .K(and_26_out), .clk(Clk), .Q(j_k_ff_9_q));  // open: Qn, preset, reset
  J_K_Flip_Flop j_k_ff_10 (.J(and_11_out), .K(and_27_out), .clk(Clk), .Q(j_k_ff_10_q));  // open: Qn, preset, reset
  J_K_Flip_Flop j_k_ff_11 (.J(and_12_out), .K(and_28_out), .clk(Clk), .Q(j_k_ff_11_q));  // open: Qn, preset, reset
  J_K_Flip_Flop j_k_ff_12 (.J(and_13_out), .K(and_29_out), .clk(Clk), .Q(j_k_ff_12_q));  // open: Qn, preset, reset
  J_K_Flip_Flop j_k_ff_13 (.J(and_14_out), .K(and_30_out), .clk(Clk), .Q(j_k_ff_13_q));  // open: Qn, preset, reset
  J_K_Flip_Flop j_k_ff_14 (.J(and_15_out), .K(and_31_out), .clk(Clk), .Q(j_k_ff_14_q));  // open: Qn, preset, reset
  J_K_Flip_Flop j_k_ff_15 (.J(and_16_out), .K(and_32_out), .clk(Clk), .Q(j_k_ff_15_q));  // open: Qn, preset, reset
  J_K_Flip_Flop j_k_ff_16 (.J(and_17_out), .K(and_33_out), .clk(Clk), .Q(j_k_ff_16_q));  // open: Qn, preset, reset
  and and_35 (DataOut[0], and_34_out, Clk, j_k_ff_1_q);
  and and_36 (DataOut[1], and_34_out, Clk, j_k_ff_2_q);
  and and_37 (DataOut[2], and_34_out, Clk, j_k_ff_3_q);
  and and_38 (DataOut[3], and_34_out, Clk, j_k_ff_4_q);
  and and_39 (DataOut[4], and_34_out, Clk, j_k_ff_5_q);
  and and_40 (DataOut[5], and_34_out, Clk, j_k_ff_6_q);
  and and_41 (DataOut[6], and_34_out, Clk, j_k_ff_7_q);
  and and_42 (DataOut[7], and_34_out, Clk, j_k_ff_8_q);
  and and_43 (DataOut[8], and_34_out, Clk, j_k_ff_9_q);
  and and_44 (DataOut[9], and_34_out, Clk, j_k_ff_10_q);
  and and_45 (DataOut[10], and_34_out, Clk, j_k_ff_11_q);
  and and_46 (DataOut[11], and_34_out, Clk, j_k_ff_12_q);
  and and_47 (DataOut[12], and_34_out, Clk, j_k_ff_13_q);
  and and_48 (DataOut[13], and_34_out, Clk, j_k_ff_14_q);
  and and_49 (DataOut[14], and_34_out, Clk, j_k_ff_15_q);
  and and_50 (DataOut[15], and_34_out, Clk, j_k_ff_16_q);
endmodule

module sixteenRAMsixteenB (
  input  Clk,
  input  OE,
  input  WE,
  input  [15:0] DataIn,
  input  [3:0] Address,
  output [15:0] DataOut
);

  wire and_1_out, and_2_out, and_3_out, and_4_out, and_5_out, and_6_out, and_7_out, and_8_out, and_9_out,
       and_10_out, and_11_out, and_12_out, and_13_out, and_14_out, and_15_out, and_16_out,
       demultiplexer_1_out0, demultiplexer_1_out1, demultiplexer_1_out2, demultiplexer_1_out3,
       demultiplexer_1_out4, demultiplexer_1_out5, demultiplexer_1_out6, demultiplexer_1_out7,
       demultiplexer_1_out8, demultiplexer_1_out9, demultiplexer_1_out10, demultiplexer_1_out11,
       demultiplexer_1_out12, demultiplexer_1_out13, demultiplexer_1_out14, demultiplexer_1_out15;
  wire [15:0] sixteenregister_1_dataout, sixteenregister_2_dataout, sixteenregister_3_dataout,
       sixteenregister_4_dataout, sixteenregister_5_dataout, sixteenregister_6_dataout,
       sixteenregister_7_dataout, sixteenregister_8_dataout, sixteenregister_9_dataout,
       sixteenregister_10_dataout, sixteenregister_11_dataout, sixteenregister_12_dataout,
       sixteenregister_13_dataout, sixteenregister_14_dataout, sixteenregister_15_dataout,
       sixteenregister_16_dataout;

  and and_1 (and_1_out, OE, demultiplexer_1_out0);
  and and_2 (and_2_out, OE, demultiplexer_1_out1);
  and and_3 (and_3_out, OE, demultiplexer_1_out2);
  and and_4 (and_4_out, OE, demultiplexer_1_out3);
  and and_5 (and_5_out, OE, demultiplexer_1_out4);
  and and_6 (and_6_out, OE, demultiplexer_1_out5);
  and and_7 (and_7_out, OE, demultiplexer_1_out6);
  sixteenRegister sixteenregister_1 (
    .WriteEnable(WE), .Clk(Clk), .OutputEnable(OE), .Selected(demultiplexer_1_out15), .DataIn(DataIn),
    .DataOut(sixteenregister_1_dataout));
  sixteenRegister sixteenregister_2 (
    .WriteEnable(WE), .Clk(Clk), .OutputEnable(OE), .Selected(demultiplexer_1_out14), .DataIn(DataIn),
    .DataOut(sixteenregister_2_dataout));
  sixteenRegister sixteenregister_3 (
    .WriteEnable(WE), .Clk(Clk), .OutputEnable(OE), .Selected(demultiplexer_1_out13), .DataIn(DataIn),
    .DataOut(sixteenregister_3_dataout));
  sixteenRegister sixteenregister_4 (
    .WriteEnable(WE), .Clk(Clk), .OutputEnable(OE), .Selected(demultiplexer_1_out12), .DataIn(DataIn),
    .DataOut(sixteenregister_4_dataout));
  sixteenRegister sixteenregister_5 (
    .WriteEnable(WE), .Clk(Clk), .OutputEnable(OE), .Selected(demultiplexer_1_out11), .DataIn(DataIn),
    .DataOut(sixteenregister_5_dataout));
  sixteenRegister sixteenregister_6 (
    .WriteEnable(WE), .Clk(Clk), .OutputEnable(OE), .Selected(demultiplexer_1_out10), .DataIn(DataIn),
    .DataOut(sixteenregister_6_dataout));
  sixteenRegister sixteenregister_7 (
    .WriteEnable(WE), .Clk(Clk), .OutputEnable(OE), .Selected(demultiplexer_1_out9), .DataIn(DataIn),
    .DataOut(sixteenregister_7_dataout));
  sixteenRegister sixteenregister_8 (
    .WriteEnable(WE), .Clk(Clk), .OutputEnable(OE), .Selected(demultiplexer_1_out8), .DataIn(DataIn),
    .DataOut(sixteenregister_8_dataout));
  sixteenRegister sixteenregister_9 (
    .WriteEnable(WE), .Clk(Clk), .OutputEnable(OE), .Selected(demultiplexer_1_out7), .DataIn(DataIn),
    .DataOut(sixteenregister_9_dataout));
  sixteenRegister sixteenregister_10 (
    .WriteEnable(WE), .Clk(Clk), .OutputEnable(OE), .Selected(demultiplexer_1_out6), .DataIn(DataIn),
    .DataOut(sixteenregister_10_dataout));
  sixteenRegister sixteenregister_11 (
    .WriteEnable(WE), .Clk(Clk), .OutputEnable(OE), .Selected(demultiplexer_1_out5), .DataIn(DataIn),
    .DataOut(sixteenregister_11_dataout));
  sixteenRegister sixteenregister_12 (
    .WriteEnable(WE), .Clk(Clk), .OutputEnable(OE), .Selected(demultiplexer_1_out4), .DataIn(DataIn),
    .DataOut(sixteenregister_12_dataout));
  sixteenRegister sixteenregister_13 (
    .WriteEnable(WE), .Clk(Clk), .OutputEnable(OE), .Selected(demultiplexer_1_out3), .DataIn(DataIn),
    .DataOut(sixteenregister_13_dataout));
  sixteenRegister sixteenregister_14 (
    .WriteEnable(WE), .Clk(Clk), .OutputEnable(OE), .Selected(demultiplexer_1_out2), .DataIn(DataIn),
    .DataOut(sixteenregister_14_dataout));
  sixteenRegister sixteenregister_15 (
    .WriteEnable(WE), .Clk(Clk), .OutputEnable(OE), .Selected(demultiplexer_1_out1), .DataIn(DataIn),
    .DataOut(sixteenregister_15_dataout));
  sixteenRegister sixteenregister_16 (
    .WriteEnable(WE), .Clk(Clk), .OutputEnable(OE), .Selected(demultiplexer_1_out0), .DataIn(DataIn),
    .DataOut(sixteenregister_16_dataout));
  Demultiplexer #(.select(4)) demultiplexer_1 (
    .out0(demultiplexer_1_out0), .out1(demultiplexer_1_out1), .out2(demultiplexer_1_out2),
    .out3(demultiplexer_1_out3), .out4(demultiplexer_1_out4), .out5(demultiplexer_1_out5),
    .out6(demultiplexer_1_out6), .out7(demultiplexer_1_out7), .out8(demultiplexer_1_out8),
    .out9(demultiplexer_1_out9), .out10(demultiplexer_1_out10), .out11(demultiplexer_1_out11),
    .out12(demultiplexer_1_out12), .out13(demultiplexer_1_out13), .out14(demultiplexer_1_out14),
    .out15(demultiplexer_1_out15), .in(1'b1), .sel(Address));
  and and_8 (and_8_out, OE, demultiplexer_1_out7);
  and and_9 (and_9_out, OE, demultiplexer_1_out8);
  and and_10 (and_10_out, OE, demultiplexer_1_out9);
  and and_11 (and_11_out, OE, demultiplexer_1_out11);
  and and_12 (and_12_out, OE, demultiplexer_1_out10);
  assign DataOut = and_16_out ? sixteenregister_1_dataout : 16'bz;  // Controlled_Buffer controlled_buffer_1
  assign DataOut = and_15_out ? sixteenregister_2_dataout : 16'bz;  // Controlled_Buffer controlled_buffer_2
  assign DataOut = and_14_out ? sixteenregister_3_dataout : 16'bz;  // Controlled_Buffer controlled_buffer_3
  assign DataOut = and_13_out ? sixteenregister_4_dataout : 16'bz;  // Controlled_Buffer controlled_buffer_4
  assign DataOut = and_11_out ? sixteenregister_5_dataout : 16'bz;  // Controlled_Buffer controlled_buffer_5
  assign DataOut = and_12_out ? sixteenregister_6_dataout : 16'bz;  // Controlled_Buffer controlled_buffer_6
  assign DataOut = and_10_out ? sixteenregister_7_dataout : 16'bz;  // Controlled_Buffer controlled_buffer_7
  assign DataOut = and_9_out ? sixteenregister_8_dataout : 16'bz;  // Controlled_Buffer controlled_buffer_8
  assign DataOut = and_8_out ? sixteenregister_9_dataout : 16'bz;  // Controlled_Buffer controlled_buffer_9
  assign DataOut = and_7_out ? sixteenregister_10_dataout : 16'bz;  // Controlled_Buffer controlled_buffer_10
  assign DataOut = and_6_out ? sixteenregister_11_dataout : 16'bz;  // Controlled_Buffer controlled_buffer_11
  assign DataOut = and_5_out ? sixteenregister_12_dataout : 16'bz;  // Controlled_Buffer controlled_buffer_12
  assign DataOut = and_4_out ? sixteenregister_13_dataout : 16'bz;  // Controlled_Buffer controlled_buffer_13
  assign DataOut = and_3_out ? sixteenregister_14_dataout : 16'bz;  // Controlled_Buffer controlled_buffer_14
  assign DataOut = and_2_out ? sixteenregister_15_dataout : 16'bz;  // Controlled_Buffer controlled_buffer_15
  assign DataOut = and_1_out ? sixteenregister_16_dataout : 16'bz;  // Controlled_Buffer controlled_buffer_16
  and and_13 (and_13_out, OE, demultiplexer_1_out12);
  and and_14 (and_14_out, OE, demultiplexer_1_out13);
  and and_15 (and_15_out, OE, demultiplexer_1_out14);
  and and_16 (and_16_out, OE, demultiplexer_1_out15);

  // Notes on the sheet:
  //   0xf
  //   0x0
endmodule
